# Fritzing sketch nano connections (saved by Fritzing 0.8.7b)
breadboards: 1

parts:
  Part1 = Arduino Nano (Rev3.0) (ICSP)
  Part2 = 9 Degrees of Freedom - Sensor Stick
  Part3 = Breakout Board for Electret Microphone
  U1 = HC-05 Bluetooth Transceiver Breakout Board, 5V, 6pin [package=SIP]
  VCC1 = Battery block 9V

nets:
  N1: Part1.D1/TX, U1.TX
  GND: Part1.GND, Part2.GND, Part3.GND, U1.GND, VCC1.-
  N2: Part1.VIN, VCC1.+
  VCC: Part1.5V, Part3.VCC, U1.VCC
  N3: Part1.A5, Part2.SCL
  N4: Part1.A4, Part2.SDA
  N5: Part1.A1, Part3.AUD
  3V3: Part1.3V3, Part2.VCC

notes:
  Pololu AltIMU-10
  Sparkfun Electret Microphone Breakout
  HC-06 serial bluetooth module

custom parts:
  HC-05 Bluetooth Transceiver Breakout Board, 5V, 6pin: Breakout board for HC-05 with 5V-to-3V translation, command mode pin (KEY) and STATE pin. http://www.ebay.com/itm/HC-05-Bluetooth-Transceiver-Host-Slave-Master-Module-Wireless-Serial-6pin-/221158958927?pt=LH_DefaultDomain_0&hash=item337e19e74f
